// Logisim project CircuitComplex.circ as structural Verilog: 4 circuits, main circuit UAL
module UAL (
  input  INVERSa,
  input  Tin,
  input  a,
  input  enable,
  input  b,
  input  enable_b,
  input  s0,
  input  s1,
  output out_9,
  output out_10
);

  wire and_1_out, and_2_out, decodor_1_d0, decodor_1_d1, decodor_1_d2, decodor_1_d3, sumator_complet_1_s,
       unitate_logica_1_s0, unitate_logica_1_s1, unitate_logica_1_s2, xor_1_out;

  decodor decodor_1 (.S0(s0), .S1(s1), .D0(decodor_1_d0), .D1(decodor_1_d1), .D2(decodor_1_d2), .D3(decodor_1_d3));
  and and_1 (and_1_out, a, enable);
  and and_2 (and_2_out, b, enable_b);
  xor xor_1 (xor_1_out, INVERSa, and_1_out);
  unitate_logica unitate_logica_1 (
    .a(xor_1_out), .b(and_2_out), .D0(decodor_1_d0), .D1(decodor_1_d1), .D2(decodor_1_d2),
    .s2(unitate_logica_1_s2), .s1(unitate_logica_1_s1), .s0(unitate_logica_1_s0));
  sumator_complet sumator_complet_1 (
    .b(and_2_out), .a(and_1_out), .D3(decodor_1_d3), .Tin(Tin), .Tout(out_10), .S(sumator_complet_1_s));
  or or_1 (out_9, unitate_logica_1_s2, unitate_logica_1_s1, unitate_logica_1_s0, sumator_complet_1_s);
endmodule

// UL
module unitate_logica (
  input  a,
  input  b,
  input  D0,
  input  D1,
  input  D2,
  output s2,
  output s1,
  output s0
);

  wire and_1_out, not_1_out, or_1_out;

  and and_1 (and_1_out, a, b);
  or or_1 (or_1_out, a, b);
  not not_1 (not_1_out, b);
  and and_2 (s2, and_1_out, D0);
  and and_3 (s1, or_1_out, D1);
  and and_4 (s0, not_1_out, D2);
endmodule

// dec
module decodor (
  input  S0,
  input  S1,
  output D0,
  output D1,
  output D2,
  output D3
);

  wire not_1_out, not_2_out, not_3_out, not_4_out;

  not not_1 (not_1_out, S0);
  not not_2 (not_2_out, S1);
  not not_3 (not_3_out, S0);
  not not_4 (not_4_out, S1);
  and _00 (D0, not_3_out, not_4_out);
  and _01 (D1, not_1_out, S1);
  and _10 (D2, S0, not_2_out);
  and _11 (D3, S1, S0);
endmodule

// sumcomp
module sumator_complet (
  input  Tin,
  input  b,
  input  a,
  input  D3,
  output S,
  output Tout
);

  wire and_1_out, and_2_out, xor_1_out, xor_2_out;

  and and_1 (and_1_out, D3, a, b);
  xor xor_1 (xor_1_out, b, a);
  or or_1 (Tout, and_1_out, and_2_out);
  and and_2 (and_2_out, D3, xor_1_out, Tin);
  xor xor_2 (xor_2_out, Tin, xor_1_out);
  and and_3 (S, xor_2_out, D3);
endmodule
