// Logisim project Problema4.circ as structural Verilog: 2 circuits, main circuit semisumator
module semisumator (
  input  in_1,
  input  in_2,
  output s0,
  output T0
);

  xor xor_1 (s0, in_1, in_2);
  and and_1 (T0, in_1, in_2);

  // Notes on the sheet:
  //   T = a AND b
  //   s = a XOR b
endmodule

module Sumator (
  input  a,
  input  b,
  input  c,
  output S,
  output T
);

  wire SEMISUM_s0, SEMISUM_t0, semisumator_1_t0;

  semisumator SEMISUM (.in_1(a), .in_2(b), .s0(SEMISUM_s0), .T0(SEMISUM_t0));
  semisumator semisumator_1 (.in_1(SEMISUM_s0), .in_2(c), .s0(S), .T0(semisumator_1_t0));
  or or_1 (T, semisumator_1_t0, SEMISUM_t0);

  // Notes on the sheet:
  //   T = x AND y OR z AND (x XOR y)
  //   s = a XOR b XOR c
endmodule
