// Logisim project clc.circ as structural Verilog: 3 circuits, main circuit mux2x1
module mux2x1 (
  input  a,
  input  b,
  input  select,
  output out
);

  wire _0_out, _1_out, not_1_out;

  not not_1 (not_1_out, select);
  and _0 (_0_out, a, not_1_out);
  and _1 (_1_out, b, select);
  or or_1 (out, _0_out, _1_out);

  // Notes on the sheet:
  //   (a and not s) or (b and s)
  //   (cand s=0 => a, cand s=1 => b)
endmodule

module mux8x1 (
  input  d0,
  input  d1,
  input  d2,
  input  d3,
  input  d4,
  input  d5,
  input  d6,
  input  d7,
  input  s1,
  input  s2,
  input  s3,
  output out
);

  wire _000_out, _001_out, _010_out, _011_out, _100_out, _101_out, _110_out, _111_out, not_1_out, not_2_out,
       not_3_out;

  not not_1 (not_1_out, s1);
  not not_2 (not_2_out, s2);
  not not_3 (not_3_out, s3);
  and _000 (_000_out, d0, not_1_out, not_2_out, not_3_out);
  and _001 (_001_out, d1, not_1_out, not_2_out, s3);
  and _010 (_010_out, d2, not_1_out, s2, not_3_out);
  and _011 (_011_out, d3, not_1_out, s2, s3);
  and _100 (_100_out, d4, s1, not_2_out, not_3_out);
  and _101 (_101_out, d5, s1, not_2_out, s3);
  and _110 (_110_out, d6, s1, s2, not_3_out);
  and _111 (_111_out, d7, s1, s2, s3);
  or or_1 (out, _000_out, _001_out, _010_out, _011_out, _100_out, _101_out, _110_out, _111_out);
endmodule

module mux16x1 (
  input  i0,
  input  i1,
  input  i2,
  input  i3,
  input  i4,
  input  i5,
  input  i6,
  input  i7,
  input  s3,
  input  s2,
  input  s1,
  input  s0,
  input  i8,
  input  i9,
  input  i10,
  input  i11,
  input  i12,
  input  i13,
  input  i14,
  input  i15,
  output out
);

  wire mux8x1_1_out, mux8x1_2_out;

  mux8x1 mux8x1_1 (
    .d0(i0), .d1(i1), .d2(i2), .d3(i3), .d4(i4), .d5(i5), .d6(i6), .d7(i7), .s1(s3), .s2(s2), .s3(s1),
    .out(mux8x1_1_out));
  mux8x1 mux8x1_2 (
    .d0(i8), .d1(i9), .d2(i10), .d3(i11), .d4(i12), .d5(i13), .d6(i14), .d7(i15), .s1(s3), .s2(s2), .s3(s1),
    .out(mux8x1_2_out));
  mux2x1 mux2x1_1 (.a(mux8x1_1_out), .b(mux8x1_2_out), .select(s0), .out(out));
endmodule
