// Logisim project cls.circ as structural Verilog: 7 circuits, main circuit SR-sinc
module SR_sinc (
  input  s,
  input  clock,
  input  r,
  output Q,
  output Q_prime
);

  wire and_1_out, and_2_out;

  and and_1 (and_1_out, s, clock);
  and and_2 (and_2_out, clock, r);
  SR sr_1 (.s(and_1_out), .r(and_2_out), .Q(Q), .Q_prime(Q_prime));
endmodule

module SR (
  input  s,
  input  r,
  output Q,
  output Q_prime
);

  nor nor_1 (Q, r, Q_prime);
  nor nor_2 (Q_prime, Q, s);
endmodule

module D_SR (
  input  D,
  input  clock,
  output out_3,
  output out_4
);

  wire not_1_out;

  not not_1 (not_1_out, D);
  SR_sinc sr_sinc_1 (.s(D), .clock(clock), .r(not_1_out), .Q(out_3), .Q_prime(out_4));
endmodule

module SR_sincron (
  input  in_1,
  input  in_2,
  input  in_3
);

  wire and_1_out;

  and and_1 (and_1_out, in_1, in_2);
  // AND_Gate and_2 has open pins: in0=in_2, in1=in_3, out=open
endmodule

module main (
  input  s,
  input  r,
  input  d,
  output Q,
  output Q_prime,
  output Qd,
  output Qd_prime
);

  wire clock_out;

  Clock clock (.out(clock_out));
  SR_sinc sr_sinc_1 (.s(s), .clock(clock_out), .r(r), .Q(Q), .Q_prime(Q_prime));
  D_SR d_sr_1 (.D(d), .clock(clock_out), .out_3(Qd), .out_4(Qd_prime));
endmodule

module D2 (
  input  d,
  input  clock,
  output out_3,
  output out_4
);

  wire and_1_out, not_1_out;

  and and_1 (and_1_out, d, clock);
  not not_1 (not_1_out, and_1_out);
  SR sr_1 (.s(and_1_out), .r(not_1_out), .Q(out_3), .Q_prime(out_4));
endmodule

module D (
  input  D,
  input  clock,
  output Q,
  output Q_prime
);

  wire nand_1_out, nand_2_out, not_1_out;

  not not_1 (not_1_out, D);
  nand nand_1 (nand_1_out, D, clock);
  nand nand_2 (nand_2_out, clock, not_1_out);
  nand nand_3 (Q_prime, Q, nand_2_out);
  nand nand_4 (Q, nand_1_out, Q_prime);
endmodule
