// Logisim project prob decodoare.circ as structural Verilog: 2 circuits, main circuit decodorNOR
// dec2x4
module decodorNOR (
  input  Enable,
  input  a,
  input  b,
  output ab,
  output ab_prime,
  output a_prime_b,
  output a_prime_b_prime
);

  wire not_1_out, not_2_out;

  not not_1 (not_1_out, a);
  not not_2 (not_2_out, b);
  nor nor_1 (a_prime_b_prime, a, Enable, b);
  nor nor_2 (ab, not_1_out, Enable, not_2_out);
  nor nor_3 (ab_prime, not_1_out, Enable, b);
  nor nor_4 (a_prime_b, a, Enable, not_2_out);

  // Notes on the sheet:
  //   2^2 iesiri
endmodule

module decodor3x8 (
  input  a,
  input  b,
  input  c,
  output a_prime_b_prime_c_prime,
  output abc_prime,
  output ab_prime_c,
  output ab_prime_c_prime,
  output a_prime_bc,
  output a_prime_bc_prime,
  output a_prime_b_prime_c,
  output a_prime_b_prime_c_prime_2
);

  wire not_1_out;

  not not_1 (not_1_out, a);
  decodorNOR decodornor_1 (
    .Enable(not_1_out), .a(b), .b(c), .ab(a_prime_b_prime_c_prime), .ab_prime(abc_prime),
    .a_prime_b(ab_prime_c), .a_prime_b_prime(ab_prime_c_prime));
  decodorNOR decodornor_2 (
    .Enable(a), .a(b), .b(c), .ab(a_prime_bc), .ab_prime(a_prime_bc_prime), .a_prime_b(a_prime_b_prime_c),
    .a_prime_b_prime(a_prime_b_prime_c_prime_2));
endmodule
