// Logisim project registru de deplasare.circ as structural Verilog: 2 circuits, main circuit D
module D (
  input  D,
  input  clock,
  output Q,
  output Q_prime
);

  wire nand_1_out, nand_2_out, not_1_out;

  not not_1 (not_1_out, D);
  nand nand_1 (nand_1_out, D, clock);
  nand nand_2 (nand_2_out, clock, not_1_out);
  nand nand_3 (Q, nand_1_out, Q_prime);
  nand nand_4 (Q_prime, Q, nand_2_out);
endmodule

module registru (
  input  serial_input,
  output serial_output
);

  wire clock_out, d_1_q, d_2_q, d_3_q;

  Clock clock (.out(clock_out));
  D d_1 (.D(serial_input), .clock(clock_out), .Q(d_1_q));  // open: Q_prime
  D d_2 (.D(d_1_q), .clock(clock_out), .Q(d_2_q));  // open: Q_prime
  D d_3 (.D(d_2_q), .clock(clock_out), .Q(d_3_q));  // open: Q_prime
  D d_4 (.D(d_3_q), .clock(clock_out), .Q(serial_output));  // open: Q_prime
endmodule
