// Logisim project sistemlogic1.circ as structural Verilog: 1 circuit, main circuit main
module main (
  input  in_1,
  input  in_2,
  input  in_3,
  input  in_4,
  input  in_5,
  input  in_6,
  input  in_7,
  input  in_8,
  input  in_9,
  input  in_10,
  input  in_11,
  output out_12,
  output out_13,
  output out_14,
  output out_15,
  output out_16,
  output out_17
);

  wire xor_1_out;

  xor xor_1 (xor_1_out, in_4, in_6);
  xor xor_2 (out_13, in_2, xor_1_out);
  not not_1 (out_15, in_7);
  and and_1 (out_17, in_10, in_11);
  and and_2 (out_12, in_1, in_3);
  xor xor_3 (out_14, in_3, in_5);
  or or_1 (out_16, in_8, in_9);
endmodule
