// Logisim project tema sumatoare.circ as structural Verilog: 2 circuits, main circuit main
module main (
  input  A,
  input  B,
  output suma,
  output bit_tr
);

  xor xor_1 (suma, A, B);
  and and_1 (bit_tr, A, B);
endmodule

module sumator (
  input  a,
  input  b,
  input  tr,
  output suma,
  output transport_final
);

  wire semisumator_2_bit_tr, semisumator_bit_tr, semisumator_suma;

  main semisumator (.A(a), .B(b), .suma(semisumator_suma), .bit_tr(semisumator_bit_tr));
  main semisumator_2 (.A(semisumator_suma), .B(tr), .suma(suma), .bit_tr(semisumator_2_bit_tr));
  or or_1 (transport_final, semisumator_2_bit_tr, semisumator_bit_tr);
endmodule
